# Fritzing sketch Untitled Sketch 2 (saved by Fritzing 0.9.4)
breadboards: 1

parts:
  Part1 = Arduino Mega ADK (Rev3)
  HC-SR04_Sensor_1 = HC-SR04 Ultrasonic Distance Sensor
  HC-SR04_Sensor_2 = HC-SR04 Ultrasonic Distance Sensor

nets:
  VCC: Part1.5V, HC-SR04_Sensor_1.VCC, HC-SR04_Sensor_2.VCC
  N1: Part1.D50/MISO, HC-SR04_Sensor_2.ECHO
  N2: Part1.D51/MOSI, HC-SR04_Sensor_2.TRIG
  N3: Part1.D52/SCK, HC-SR04_Sensor_1.ECHO
  N4: Part1.D53/SS, HC-SR04_Sensor_1.TRIG
  GND: Part1.GND, HC-SR04_Sensor_1.GND, HC-SR04_Sensor_2.GND
